# Fritzing sketch pas_analyzer (saved by Fritzing 0.9.10b)
breadboards: 1

parts:
  Composant1 = Arduino Nano (Rev3.0)
  J1 = male pin header, 3 pins [form="♂ (male)"]

nets:
  N1: Composant1.D2, J1.pin1
  N2: Composant1.GND, J1.pin2
  N3: Composant1.5V, J1.pin3

notes:
  PAS sensor
  PAS analyzer, Chris74
  Gnd
  +5V
  signal (D2)
